// Logisim project adder_check.circ as structural Verilog: 1 circuit, main circuit main
module main (
  output [4:0] sum,
  output halt
);

  wire c1, c2, c3;

  _1bit_adder fa0 (.a(1'b1), .b(1'b0), .cin(1'b1), .s(sum[0]), .cout(c1));
  _1bit_adder fa1 (.a(1'b1), .b(1'b1), .cin(c1), .s(sum[1]), .cout(c2));
  _1bit_adder fa2 (.a(1'b0), .b(1'b1), .cin(c2), .s(sum[2]), .cout(c3));
  _1bit_adder fa3 (.a(1'b1), .b(1'b0), .cin(c3), .s(sum[3]), .cout(sum[4]));

  assign halt = 1'b1;

  // Other names for the same wires on the sheet: s0 = sum[0]; s1 = sum[1]; s2 = sum[2]; s3 = sum[3]; c4 = sum[4]
endmodule
