// Logisim project ripple_carry.circ as structural Verilog: 1 circuit, main circuit main
module main (
  input  a0,
  input  b0,
  input  cin,
  input  a1,
  input  b1,
  input  a2,
  input  b2,
  input  a3,
  input  b3,
  output s0,
  output s1,
  output s2,
  output s3,
  output cout
);

  wire c1, c2, c3;

  _1bit_adder fa0 (.a(a0), .b(b0), .cin(cin), .s(s0), .cout(c1));
  _1bit_adder fa1 (.a(a1), .b(b1), .cin(c1), .s(s1), .cout(c2));
  _1bit_adder fa2 (.a(a2), .b(b2), .cin(c2), .s(s2), .cout(c3));
  _1bit_adder fa3 (.a(a3), .b(b3), .cin(c3), .s(s3), .cout(cout));
endmodule
